# Fritzing sketch DevreSemasi (saved by Fritzing 0.9.3b)
breadboards: 1

parts:
  Parça1 = Arduino Uno (Rev3) - ICSP
  hc-sr1 = hc-sr04
  LED1 = smd LED [color="Red (633nm)" package="0603 [SMD]"]
  LED2 = smd LED [color="Red (633nm)" package="0603 [SMD]"]
  LED3 = smd LED [color="Red (633nm)" package="0603 [SMD]"]
  Parça2 = Bluetooth HC-05 Macho
  R1 = Resistor [tolerance=±5% resistance=220 package="1206 [SMD]"]
  R2 = Resistor [tolerance=±5% resistance=220 package="1206 [SMD]"]
  M1 = DC Motor
  R3 = Resistor [tolerance=±5% resistance=220 package="1206 [SMD]"]
  R4 = Resistor [tolerance=±5% resistance=330 package="2010 [SMD]"]
  Q1 = TRANSISTOR_NPN [package=to-92]
  R5 = Resistor [tolerance=±5% resistance=330 package="0805 [SMD]"]
  J1 = Piezo Speaker

nets:
  N1: Parça1.ICSP_MISO, Parça1.D12/MISO, R2.Pin_1
  N2: Parça1.D9_PWM, R5.Pin_1
  N3: Parça1.D10_PWM/SS, R3.Pin_1
  N4: Parça1.D11_PWM/MOSI, R4.Pin_1
  N5: Parça1.D13/SCK, R1.Pin_1
  N6: Parça1.D0/RX, Parça2.TXD
  N7: Parça1.D1/TX, Parça2.RXD
  N8: Parça1.D6_PWM, hc-sr1.Echo
  N9: Parça1.D7, hc-sr1.Trig
  N10: Parça1.3V3, M1.pin_1
  VCC: Parça1.5V, hc-sr1.VCC, Parça2.VCC
  GND: Parça1.GND, hc-sr1.GND, LED1.cathode, LED2.cathode, LED3.cathode, Parça2.GND, Q1.C
  N11: LED1.anode, R1.Pin_0
  N12: LED2.anode, R2.Pin_0
  N13: LED3.anode, R3.Pin_0
  N14: M1.pin_2, Q1.E
  N15: R4.Pin_0, Q1.B
  N16: R5.Pin_0, J1.pin2
